# Fritzing sketch drone (saved by Fritzing 0.8.7b)

parts:
  M1 = DOIT Esp32 DevKit v1 (30 pins long, 11 pins width) [part_number=ESP32S-PIN30]
  Part1 = InvenSense MPU6050
  A1 = u-blox NEO-6M GPS Breakout
  Transceiver1 = nRF24L01 [package=module]
  U1 = Mini-360 DC-DC Buck converter [package=THT]
  M4 = Littlebee 20A ESC
  M1_2 = Littlebee 20A ESC [part_number=4]
  M2 = Littlebee 20A ESC
  M3 = Littlebee 20A ESC
  OLED_I2C1 = OLED 128x64 I2C Monochrome Display
  VCC1 = Battery
  C1 = Electrolytic Capacitor [capacitance=1µF package="100 mil [THT, electrolytic]"]
  C2 = Tantalum Capacitor [capacitance=1μF package="100 mil [THT, tantalum]"]  # not connected
  R1 = Resistor [tolerance=±5% resistance=220 package=THT]  # not connected

nets:
  3V3: M1.3V3, Part1.VCC, OLED_I2C1.VDD
  N1: M1.D4, A1.Pin_5
  N2: M1.RX2, A1.Pin_3
  N3: M1.TX2, A1.Pin_4
  N4: M1.D5, Transceiver1.CSN
  N5: M1.D18, Transceiver1.SCK
  N6: M1.D19, Transceiver1.MISO
  N7: M1.D21, OLED_I2C1.SDA
  N8: M1.D22, OLED_I2C1.SCK
  N9: M1.D23, Transceiver1.MOSI
  N10: M1.D32, Part1.SDA
  N11: M1.D33, Part1.SCL
  N12: M1.D25, Transceiver1.CE
  N13: M1.D26, M1_2.Pin_3
  N14: M1.D27, M4.Pin_3
  N15: M1.D14, M3.Pin_3
  N16: M1.D13, M2.Pin_3
  GND: M1.GND, Part1.GND, A1.Pin_2, U1.IN+, OLED_I2C1.GND, VCC1.-
  N17: M1.VIN, A1.Pin_1, U1.IN-, VCC1.+
  N18: Transceiver1.GND, U1.OUT-, C1.-
  N19: Transceiver1.VCC, U1.OUT+, C1.+

custom parts:
  DOIT Esp32 DevKit v1 (30 pins long, 11 pins width): The DOIT Esp32 DevKit v1 is one of the development board created by DOIT to evaluate the ESP-WROOM-32 module. It is based on the ESP32 microcontroller that boasts Wifi, Bluetooth, Ethernet and Low Power support all in a single chip. (vanepp) made breadboard work, adjusted pin numbering and labels and reduced size of schematic and cleaned up pcb. This chip is 30pins long (2 x15) and 11 pins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
  nRF24L01: nRF24L01 module
  Mini-360 DC-DC Buck converter: Mini-360 DC-DC Buck converter. Tiny buck step down voltage converter, input voltage 4.75 to 23V output 1 to 17V adjustable. Available from ebay and the like.
  Littlebee 20A ESC: LittleBee 20A 2-4 LiPo Battery OPTO ESC Brushless Speed Controller for RC FPV Multicopter.
